// Logisim project Assignment1.circ as structural Verilog: 9 circuits, main circuit main
// 4-bit Alu
module main (
  input  Carry_in__ADD,
  input  Carry_in_SUB,
  input  [2:0] Selector,
  input  [3:0] A,
  input  [3:0] B,
  output [3:0] Output,
  output Zero_Flag,
  output Sign_Flag,
  output Overflow_Flag,
  output Carry_Flag,
  output out_11
);

  wire add_1_carry_out, shl_1_shifted_bit, shr_1_out_2, sub_1_carry_out, xor_2_out, xor_3_out;
  wire [3:0] add_1_output, and_1_output, not_1_output, or_1_output, shl_1_output, shr_1_output, sub_1_output,
       xor_1_output;

  Not not_1 (.A(A), .Output(not_1_output));
  Add add_1 (.A(A), .B(B), .Output(add_1_output), .Carry_in(Carry_in__ADD), .Carry_out(add_1_carry_out));
  Sub sub_1 (.A(A), .B(B), .Output(sub_1_output), .Carry_in(Carry_in_SUB), .Carry_out(sub_1_carry_out));
  And and_1 (.A(A), .B(B), .Output(and_1_output));
  Or or_1 (.A(A), .B(B), .Output(or_1_output));
  Xor xor_1 (.A(A), .B(B), .Output(xor_1_output));
  Shl shl_1 (.A(B), .Output(shl_1_output), .Shifted_Bit(shl_1_shifted_bit));
  Shr shr_1 (.A(B), .Output(shr_1_output), .out_2(shr_1_out_2));
  Multiplexer #(.select(3), .width(4), .enable("false")) multiplexer_1 (
    .in0(add_1_output), .in1(sub_1_output), .in2(and_1_output), .in3(or_1_output), .in4(not_1_output),
    .in5(xor_1_output), .in6(shl_1_output), .in7(shr_1_output), .out(Output), .sel(Selector));
  nor nor_1 (Zero_Flag, Output[0], Output[1], Output[2], Output[3]);
  xor xor_2 (xor_2_out, Carry_in__ADD, add_1_carry_out);
  or or_2 (Overflow_Flag, xor_2_out, xor_3_out);
  xor xor_3 (xor_3_out, Carry_in_SUB, sub_1_carry_out);
  or or_3 (Carry_Flag, add_1_carry_out, sub_1_carry_out);
  or or_4 (out_11, shl_1_shifted_bit, shr_1_out_2);

  assign Sign_Flag = Output[3];

  // Notes on the sheet:
  //   4-BIT ALU
  //   Add :-  000
  //   Sub:-   001
  //   And:-   010
  //   Or :-     011
  //   Not:-   100
  //   Xor:-   101
  //   Shl:-   110
  //   Shr:-   111
  //   Bit Shifted while SHL and SHR
  //   (Uses A  as input)
  //   (Uses B  as input)
  //   (Uses B  as input)
  //   Parameshor Bhandari
  //   Assignment1
  //   COSC 3327
endmodule

module Add (
  input  Carry_in,
  input  [3:0] A,
  input  [3:0] B,
  output [3:0] Output,
  output Carry_out
);

  wire adder_1_cout, adder_2_cout, adder_3_cout;

  Adder #(.width(1)) adder_1 (.a(A[0]), .b(B[0]), .out(Output[0]), .cin(Carry_in), .cout(adder_1_cout));
  Adder #(.width(1)) adder_2 (.a(A[1]), .b(B[1]), .out(Output[1]), .cin(adder_1_cout), .cout(adder_2_cout));
  Adder #(.width(1)) adder_3 (.a(A[2]), .b(B[2]), .out(Output[2]), .cin(adder_2_cout), .cout(adder_3_cout));
  Adder #(.width(1)) adder_4 (.a(A[3]), .b(B[3]), .out(Output[3]), .cin(adder_3_cout), .cout(Carry_out));

  // Notes on the sheet:
  //   4-BIT ADD
  //   Parameshor Bhandari
  //   Assignment1
  //   COSC 3327
endmodule

module Sub (
  input  Carry_in,
  input  [3:0] A,
  input  [3:0] B,
  output [3:0] Output,
  output Carry_out
);

  wire subtractor_1_bout, subtractor_2_bout, subtractor_3_bout;

  Subtractor #(.width(1)) subtractor_1 (.a(A[0]), .b(B[0]), .out(Output[0]), .bin(Carry_in), .bout(subtractor_1_bout));
  Subtractor #(.width(1)) subtractor_2 (
    .a(A[1]), .b(B[1]), .out(Output[1]), .bin(subtractor_1_bout), .bout(subtractor_2_bout));
  Subtractor #(.width(1)) subtractor_3 (
    .a(A[2]), .b(B[2]), .out(Output[2]), .bin(subtractor_2_bout), .bout(subtractor_3_bout));
  Subtractor #(.width(1)) subtractor_4 (.a(A[3]), .b(B[3]), .out(Output[3]), .bin(subtractor_3_bout), .bout(Carry_out));

  // Notes on the sheet:
  //   4-BIT SUB
  //   Parameshor Bhandari
  //   Assignment1
  //   COSC 3327
endmodule

module And (
  input  [3:0] A,
  input  [3:0] B,
  output [3:0] Output
);

  and and_1 (Output[0], A[0], B[0]);
  and and_2 (Output[1], A[1], B[1]);
  and and_3 (Output[2], A[2], B[2]);
  and and_4 (Output[3], A[3], B[3]);

  // Notes on the sheet:
  //   4-BIT AND
  //   Parameshor Bhandari
  //   Assignment1
  //   COSC 3327
endmodule

module Or (
  input  [3:0] A,
  input  [3:0] B,
  output [3:0] Output
);

  or or_1 (Output[0], A[0], B[0]);
  or or_2 (Output[1], A[1], B[1]);
  or or_3 (Output[2], A[2], B[2]);
  or or_4 (Output[3], A[3], B[3]);

  // Notes on the sheet:
  //   4-BIT OR
  //   Parameshor Bhandari
  //   Assignment1
  //   COSC 3327
endmodule

module Not (
  input  [3:0] A,
  output [3:0] Output
);

  not not_1 (Output[0], A[0]);
  not not_2 (Output[1], A[1]);
  not not_3 (Output[2], A[2]);
  not not_4 (Output[3], A[3]);

  // Notes on the sheet:
  //   4-BIT NOT
  //   Parameshor Bhandari
  //   Assignment1
  //   COSC 3327
endmodule

module Xor (
  input  [3:0] A,
  input  [3:0] B,
  output [3:0] Output
);

  xor xor_1 (Output[0], A[0], B[0]);
  xor xor_2 (Output[1], A[1], B[1]);
  xor xor_3 (Output[2], A[2], B[2]);
  xor xor_4 (Output[3], A[3], B[3]);

  // Notes on the sheet:
  //   4-BIT XOR
  //   Parameshor Bhandari
  //   Assignment1
  //   COSC 3327
endmodule

module Shl (
  input  [3:0] A,
  output [3:0] Output,
  output Shifted_Bit
);

  Shifter #(.width(1)) shifter_1 (.in(A[2]), .\dist (1'b0), .out(Output[3]));
  Shifter #(.width(1)) shifter_2 (.in(A[1]), .\dist (1'b0), .out(Output[2]));
  Shifter #(.width(1)) shifter_3 (.in(A[0]), .\dist (1'b0), .out(Output[1]));
  Shifter #(.width(1)) shifter_4 (.in(1'b0), .\dist (1'b0), .out(Output[0]));

  assign Shifted_Bit = A[3];

  // Notes on the sheet:
  //   4-BIT SHL
  //   Ground
  //   Ground
  //   Parameshor Bhandari
  //   Assignment1
  //   COSC 3327
endmodule

module Shr (
  input  [3:0] A,
  output out_2,
  output [3:0] Output
);

  Shifter #(.width(1), .shift("lr")) shifter_1 (.in(1'b0), .\dist (1'b0), .out(Output[3]));
  Shifter #(.width(1), .shift("lr")) shifter_2 (.in(A[3]), .\dist (1'b0), .out(Output[2]));
  Shifter #(.width(1), .shift("lr")) shifter_3 (.in(A[2]), .\dist (1'b0), .out(Output[1]));
  Shifter #(.width(1), .shift("lr")) shifter_4 (.in(A[1]), .\dist (1'b0), .out(Output[0]));

  assign out_2 = A[0];

  // Notes on the sheet:
  //   4-BIT SHR
  //   Ground
  //   Shifted Bit
  //   Parameshor Bhandari
  //   Assignment1
  //   COSC 3327
endmodule
